# Fritzing sketch esp-car-util (saved by Fritzing 0.9.5d)

parts:
  esp2 = ESP32 DevKitc V4
  LCD1 = 2.8" SPI TFT Module [part_number=MSP2807]
  Mod1 = KY-012 Active Buzzer Module [package="Breakout board"]
  A1 = Pcm5102A module
  esp3 = ESP32 DevKitc V4
  J1 = male pin header, 6 pins [form="♂ (male)"]

nets:
  N1: esp2.3V3, A1.Pin_6
  N2: esp2.IO25, A1.Pin_2
  N3: esp2.IO26, A1.Pin_4
  N4: esp2.IO27, A1.Pin_3
  N5: esp2.GND, J1.pin1
  5V: esp2.5V, esp3.5V
  N6: LCD1.pin1, esp3.3V3
  N7: LCD1.pin2, J1.pin5
  N8: LCD1.pin3, esp3.IO27
  N9: LCD1.pin4, esp3.IO25
  N10: LCD1.pin5, esp3.IO26
  N11: LCD1.pin6, esp3.IO14
  N12: LCD1.pin7, esp3.IO32
  N13: LCD1.pin8, esp3.IO33
  N14: LCD1.pin9, esp3.IO35
  N15: Mod1.S, esp3.IO13
  N16: Mod1.-, J1.pin6
  N17: A1.Pin_1, J1.pin4
  N18: A1.Pin_5, J1.pin3
  N19: esp3.GND, J1.pin2

custom parts:
  ESP32 DevKitc V4: ESP32-DevKitC board with ESP32-WROOM-32 module. ESP32-DevKitC V4 is a small-sized ESP32-based development board produced by Espressif. Most of the pins on the ESP module are broken out to the pin headers on the board. The pins D0, D1, D2, D3, CMD and CLK are used internally for communication between ESP32 and SPI flash memory. They are grouped on both sides near the USB connector. Avoid using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
  2.8" SPI TFT Module: A generic 2.8 inch LCD TFT 320x240 display with touchscreen and SD card slot. Uses the ILI9341 controller, like the Adafruit displays of this size uses.
  KY-012 Active Buzzer Module: Active Piezoelectric Buzzer Module KY-012, it produces single-tone sound when signal is high. (Special thanks to vanepp for fixing the PCB holes and other errors)
  Pcm5102A module: Interface I2S PCM5102A DAC Decoder GY-PCM5102 I2S Player Module for Raspberry Pi pHAT Format Board Digital PCM5102 Audio Board.
